# Fritzing sketch XBEEJoystick-half (saved by Fritzing 0.6.3b)
breadboards: 1

parts:
  C1 = Electrolytic Capacitor [capacitance=10µF package="100 mil [THT, electrolytic]"]
  J1 = Screw terminal - 2 pins [package=THT]
  C2 = Electrolytic Capacitor [capacitance=1µF package="100 mil [THT, electrolytic]"]
  Joystick1 = Thumb Joystick
  R1 = Resistor [tolerance=±5% resistance=16.4k package=THT]
  R2 = Resistor [tolerance=±5% resistance=16.4k package=THT]
  R3 = Resistor [tolerance=±5% resistance=10k package=THT]
  J2 = female pin header, 4 pins [form="♀ (female)"]  # not connected
  C3 = Ceramic Capacitor [capacitance=10µF package="200 mil [THT, multilayer]"]
  C4 = Ceramic Capacitor [capacitance=10µF package="200 mil [THT, multilayer]"]
  U2 = XBee
  U3 = Voltage_Regulator___3.3V

nets:
  GND: C1.-, J1.pin1, C2.-, Joystick1.GND, Joystick1.SEL, R1.Pin_0, R2.Pin_0, R3.Pin_0, R3.Pin_1, C3.0, C4.0, U2.GND, U2.pin18, U3.connector1
  N1: C1.+, J1.pin2, U3.connector0
  VCC: C2.+, Joystick1.VCC, U2.VCC, U2.pin14, U3.connector2
  N2: Joystick1.HORZ, R1.Pin_1, C4.1, U2.pin19
  N3: Joystick1.VERT, R2.Pin_1, C3.1, U2.pin20

notes:
  Parts List
