# Fritzing sketch XBEEJoystick-half (saved by Fritzing 0.6.3b)
breadboards: 1

parts:
  C1 = Electrolytic Capacitor [capacitance=10µF package="100 mil [THT, electrolytic]"]
  J1 = Screw terminal - 2 pins [package=THT]
  C2 = Electrolytic Capacitor [capacitance=1µF package="100 mil [THT, electrolytic]"]
  Joystick1 = Thumb Joystick
  R1 = Resistor [tolerance=±5% resistance=16.4k package=THT]
  R2 = Resistor [tolerance=±5% resistance=16.4k package=THT]
  R3 = Resistor [tolerance=±5% resistance=10k package=THT]
  J2 = female pin header, 4 pins [form="♀ (female)"]  # not connected
  C3 = Ceramic Capacitor [capacitance=10µF package="200 mil [THT, multilayer]"]
  C4 = Ceramic Capacitor [capacitance=10µF package="200 mil [THT, multilayer]"]
  U2 = XBee
  U3 = Voltage Regulator - 3.3V [package="TO220 [THT]"]
  R4 = Resistor [tolerance=±5% resistance=100 package=THT]

nets:
  GND: C1.-, J1.pin1, C2.-, Joystick1.GND, Joystick1.SEL, R1.Pin_0, R2.Pin_0, R3.Pin_1, C3.0, C4.0, U2.GND, U3.GND, R4.Pin_0
  N1: C1.+, J1.pin2, U3.input_voltage
  VCC: C2.+, Joystick1.VCC, R3.Pin_0, U2.VCC, U2.pin14, U3.output_voltage
  N2: Joystick1.HORZ, R1.Pin_1, C4.1, U2.pin19
  N3: Joystick1.VERT, R2.Pin_1, C3.1, U2.pin20
  N4: U2.pin18, R4.Pin_1

notes:
  Bill of Materials: XBEEJoystick-half.fz
  /Users/rianders/projects/Xbee-Joystick-Control/fritzing/XBEEJoystick-half.fz
  Sunday, November 20 2011, 21:58:28
  Assembly List
  Label Part Type Properties
  C1 Electrolytic Capacitor package 100 mil [THT, electrolytic]; capacitance 10µF; voltage 6.3V
  C2 Electrolytic Capacitor package 100 mil [THT, electrolytic]; capacitance 1µF; voltage 6.3V
  C3 Ceramic Capacitor package 200 mil [THT, multilayer]; capacitance 10µF; voltage 6.3V
  C4 Ceramic Capacitor package 200 mil [THT, multilayer]; capacitance 10µF; voltage 6.3V
  J1 Screw terminal - 2 pins package THT; pins 2; pin spacing 0.1in (2.54mm)
  J2 Generic female header - 4 pins package THT; form ♀ (female); pins 4; pin spacing 0.1in (2.54mm)
  Joystick1 Thumb Joystick
  R1 220 Ω Resistor package THT; tolerance ±5%; resistance 16.4kΩ; pin spacing 400 mil
  R2 220 Ω Resistor package THT; tolerance ±5%; resistance 16.4kΩ; pin spacing 400 mil
  R3 220 Ω Resistor package THT; tolerance ±5%; resistance 10kΩ; pin spacing 400 mil
  R4 220 Ω Resistor package THT; tolerance ±5%; resistance 100Ω; pin spacing 400 mil
  U2 XBee model XBee ZNet 2.5; pins 20
  U3 Voltage Regulator - 3.3V package TO220 [THT]; voltage 3.3V
  Shopping List
  Amount Part Type Properties
  4 220 Ω Resistor package THT; tolerance ±5%; resistance 16.4kΩ; pin spacing 400 mil
  2 Ceramic Capacitor package 200 mil [THT, multilayer]; capacitance 10µF; voltage 6.3V
  2 Electrolytic Capacitor package 100 mil [THT, electrolytic]; capacitance 10µF; voltage 6.3V
  1 Generic female header - 4 pins package THT; form ♀ (female); pins 4; pin spacing 0.1in (2.54mm)
  1 Screw terminal - 2 pins package THT; pins 2; pin spacing 0.1in (2.54mm)
  1 Thumb Joystick
  1 Voltage Regulator - 3.3V package TO220 [THT]; voltage 3.3V
  1 XBee model XBee ZNet 2.5; pins 20
  Exported with Fritzing 0.6.3- http://fritzing.org

custom parts:
  Voltage Regulator - 3.3V: 3.3V DC Voltage Regulator
