# Fritzing sketch XbeeArduinoConnectionShield (saved by Fritzing 0.6.3b)

parts:
  U1 = XBee
  Arduino1 = Arduino

nets:
  VCC: U1.VCC, Arduino1.3V3
  N1: U1.pin2, Arduino1.D0RX
  N2: U1.pin3, Arduino1.D1TX
  GND: U1.GND, Arduino1.GND
