# Fritzing sketch XbeeArduinoConnectionShieldA (saved by Fritzing 0.6.4b)

parts:
  U1 = XBee
  J1 = female pin header, 2 pins [form="♀ (female)"]
  J2 = female pin header, 2 pins [form="♀ (female)"]
  J3 = female pin header, 2 pins [form="♀ (female)"]
  J4 = female pin header, 2 pins [form="♀ (female)"]
  J5 = female pin header, 2 pins [form="♀ (female)"]
  Arduino1 = Arduino

nets:
  VCC: U1.VCC, Arduino1.3V3
  N1: U1.pin2, J2.pin2, J5.pin2
  N2: U1.pin3, J1.pin2, J4.pin2
  GND: U1.GND, Arduino1.GND
  N3: J1.pin1, Arduino1.D1TX
  N4: J2.pin1, Arduino1.D0RX
  N5: J3.pin1, J4.pin1
  N6: J3.pin2, J5.pin1
