# Fritzing sketch XbeeBreakOutStatusLED (saved by Fritzing 0.6.3b)

parts:
  U1 = XBee
  J1 = female pin header, 10 pins [form="♀ (female)"]
  J2 = female pin header, 10 pins [form="♀ (female)"]

nets:
  N1: U1.VCC, J2.pin1
  N2: U1.pin2, J2.pin2
  N3: U1.pin3, J2.pin3
  N4: U1.pin4, J2.pin4
  N5: U1.pin5, J2.pin5
  N6: U1.pin6, J2.pin6
  N7: U1.pin7, J2.pin7
  N8: U1.pin8, J2.pin8
  N9: U1.pin9, J2.pin9
  N10: U1.GND, J2.pin10
  N11: U1.pin11, J1.pin10
  N12: U1.pin12, J1.pin9
  N13: U1.pin13, J1.pin8
  N14: U1.pin14, J1.pin7
  N15: U1.pin15, J1.pin6
  N16: U1.pin16, J1.pin5
  N17: U1.pin17, J1.pin4
  N18: U1.pin18, J1.pin3
  N19: U1.pin19, J1.pin2
  N20: U1.pin20, J1.pin1
