# Fritzing sketch XbeeFubarinoConnectionShield (saved by Fritzing 0.7.4b)

parts:
  U1 = XBee
  FubarinoSD1 = IC, DIP package, 56 pins [chip_label=FubarinoSD spacing=900mil]
  IC1 = L293D [package=THT]
  M1 = Screw terminal - 2 pins [package=THT]
  M2 = Screw terminal - 2 pins [package=THT]
  M3 = Screw terminal - 2 pins [package=THT]
  IC2 = L293D [package=THT]
  U2 = Voltage Regulator - 5V [package="TO220 [THT]"]
  M4 = Screw terminal - 2 pins [package=THT]
  C1 = Electrolytic Capacitor [capacitance=100nF package="100 mil [THT, electrolytic]"]
  C2 = Electrolytic Capacitor [capacitance=100nF package="100 mil [THT, electrolytic]"]
  P1 = Screw terminal - 2 pins [package=THT]

nets:
  N1: U1.VCC, FubarinoSD1.pin2
  N2: U1.pin2, FubarinoSD1.pin52
  N3: U1.pin3, FubarinoSD1.pin53
  GND: U1.GND, FubarinoSD1.pin29, FubarinoSD1.pin56, IC1.0V, IC1.+Vmotor, IC2.0V, IC2.+Vmotor, U2.GND, C1.-, C2.-, P1.pin1
  N4: FubarinoSD1.pin4, IC2.Enable_1
  N5: FubarinoSD1.pin5, IC2.In_2
  N6: FubarinoSD1.pin6, IC2.In_4
  N7: FubarinoSD1.pin7, IC2.Enable_2
  N8: FubarinoSD1.pin11, IC2.In_3
  N9: FubarinoSD1.pin12, IC2.In_1
  N10: FubarinoSD1.pin13, IC1.In_1
  N11: FubarinoSD1.pin14, IC1.In_3
  N12: FubarinoSD1.pin18, IC1.Enable_1
  N13: FubarinoSD1.pin19, IC1.In_2
  N14: FubarinoSD1.pin20, IC1.Enable_2
  N15: FubarinoSD1.pin21, IC1.In_4
  5V: FubarinoSD1.pin55, IC1.+V, IC2.+V, U2.output_voltage, C2.+
  N16: IC1.Out_1_(_Controlled_by_Enable_1_), M3.pin2
  N17: IC1.Out_2_(_Controlled_by_Enable_1_), M3.pin1
  N18: IC1.Out_3_(_Controlled_by_Enable_2_), M4.pin2
  N19: IC1.Out_4_(_Controlled_by_Enable_2_), M4.pin1
  N20: M1.pin1, IC2.Out_2_(_Controlled_by_Enable_1_)
  N21: M1.pin2, IC2.Out_1_(_Controlled_by_Enable_1_)
  N22: M2.pin1, IC2.Out_4_(_Controlled_by_Enable_2_)
  N23: M2.pin2, IC2.Out_3_(_Controlled_by_Enable_2_)
  N24: U2.input_voltage, C1.+, P1.pin2
